# Fritzing sketch SmartMirror (saved by Fritzing 0.8.7b)
breadboards: 1

parts:
  Raspberry_Pi_1 = Raspberry Pi 3 [part_number=RPI-3-V1.2]
  S1 = Pushbutton [package="[THT]"]
  S2 = Pushbutton [package="[THT]"]
  S3 = Pushbutton [package="[THT]"]
  S4 = Pushbutton [package="[THT]"]

nets:
  N1: Raspberry_Pi_1.GIPO24, S1.Pin_3, S1.Pin_4
  N2: Raspberry_Pi_1.GIPO23, S2.Pin_3, S2.Pin_4
  N3: Raspberry_Pi_1.GIPO18, S3.Pin_3, S3.Pin_4
  N4: Raspberry_Pi_1.GIPO15, S4.Pin_3, S4.Pin_4
  N5: Raspberry_Pi_1.GND, S1.Pin_1, S1.Pin_2, S2.Pin_1, S2.Pin_2, S3.Pin_1, S3.Pin_2, S4.Pin_1, S4.Pin_2
