# Fritzing sketch SmartMirrorV1.1 (saved by Fritzing 0.9.3b)
breadboards: 1

parts:
  Raspberry_Pi_1 = Raspberry Pi 3 [part_number=RPI-3-V1.2]
  DeleteAllIMGButton = Pushbutton [package="[THT]"]
  TakeImageButton = Pushbutton [package="[THT]"]
  ShutDownButton = Pushbutton [package="[THT]"]
  StartButton = Pushbutton [package="[THT]"]
  MirrorModeButton = Pushbutton [package="[THT]"]
  IMGForwardButton = Pushbutton [package="[THT]"]
  IMGBackButton = Pushbutton [package="[THT]"]

nets:
  N1: Raspberry_Pi_1.GIPO12, MirrorModeButton.Pin_3, MirrorModeButton.Pin_4
  N2: Raspberry_Pi_1.GIPO8, IMGForwardButton.Pin_3, IMGForwardButton.Pin_4
  N3: Raspberry_Pi_1.GIPO25, IMGBackButton.Pin_3, IMGBackButton.Pin_4
  N4: Raspberry_Pi_1.GND, DeleteAllIMGButton.Pin_1, DeleteAllIMGButton.Pin_2, TakeImageButton.Pin_1, TakeImageButton.Pin_2, ShutDownButton.Pin_1, ShutDownButton.Pin_2, StartButton.Pin_1, StartButton.Pin_2, MirrorModeButton.Pin_1, MirrorModeButton.Pin_2, IMGForwardButton.Pin_1, IMGForwardButton.Pin_2, IMGBackButton.Pin_1, IMGBackButton.Pin_2
  N5: Raspberry_Pi_1.GIPO24, DeleteAllIMGButton.Pin_3, DeleteAllIMGButton.Pin_4
  N6: Raspberry_Pi_1.GIPO23, TakeImageButton.Pin_3, TakeImageButton.Pin_4
  N7: Raspberry_Pi_1.GIPO18, ShutDownButton.Pin_3, ShutDownButton.Pin_4
  N8: Raspberry_Pi_1.GIPO15, StartButton.Pin_3, StartButton.Pin_4
