# Fritzing sketch SmartMirrorV1.2 (saved by Fritzing 0.9.3b)
breadboards: 2

parts:
  Raspberry_Pi_1 = Raspberry Pi 3 [part_number=RPI-3-V1.2]
  GalleryRightButton = Pushbutton [package="[THT]"]
  TakeImageButton = Pushbutton [package="[THT]"]
  LeaveGalleryButton = Pushbutton [package="[THT]"]
  DeleteAllImagesButton = Pushbutton [package="[THT]"]
  GalleryLeftButton = Pushbutton [package="[THT]"]
  R1 = Resistor [tolerance=±5% resistance=220 package=THT]
  R2 = Resistor [tolerance=±5% resistance=220 package=THT]
  R3 = Resistor [tolerance=±5% resistance=220 package=THT]
  R4 = Resistor [tolerance=±5% resistance=220 package=THT]
  R5 = Resistor [tolerance=±5% resistance=220 package=THT]
  StartMirrorSlideshow = Pushbutton [package="[THT]"]
  StartMirrorDefault = Pushbutton [package="[THT]"]
  ShutDownMirror = Pushbutton [package="[THT]"]
  R6 = Resistor [tolerance=±5% resistance=220 package=THT]
  R7 = Resistor [tolerance=±5% resistance=220 package=THT]
  R8 = Resistor [tolerance=±5% resistance=220 package=THT]
  PIR-Sensor = HC-SR501 Body Sensor Module

nets (from the breadboard view):
  N1: Raspberry_Pi_1.GND, GalleryRightButton.Pin_3, GalleryRightButton.Pin_4, TakeImageButton.Pin_3, TakeImageButton.Pin_4, LeaveGalleryButton.Pin_3, LeaveGalleryButton.Pin_4, DeleteAllImagesButton.Pin_3, DeleteAllImagesButton.Pin_4, GalleryLeftButton.Pin_3, GalleryLeftButton.Pin_4
  N2: Raspberry_Pi_1.GIPO20, R1.Pin_1
  N3: Raspberry_Pi_1.GIPO16, PIR-Sensor.OUT
  N4: Raspberry_Pi_1.GIPO12, R6.Pin_1
  N5: Raspberry_Pi_1.GIPO7, R2.Pin_1
  N6: Raspberry_Pi_1.GIPO8, R4.Pin_1
  N7: Raspberry_Pi_1.GIPO24, R5.Pin_1
  N8: Raspberry_Pi_1.GIPO23, R3.Pin_1
  N9: Raspberry_Pi_1.GIPO18, R8.Pin_1
  N10: Raspberry_Pi_1.GIPO15, R7.Pin_1
  N11: Raspberry_Pi_1.GIPO14, PIR-Sensor.GND
  5V: Raspberry_Pi_1.5V, PIR-Sensor.VCC
  N12: GalleryRightButton.Pin_1, GalleryRightButton.Pin_2, R2.Pin_0
  N13: TakeImageButton.Pin_1, TakeImageButton.Pin_2, R3.Pin_0
  N14: LeaveGalleryButton.Pin_1, LeaveGalleryButton.Pin_2, R1.Pin_0
  N15: DeleteAllImagesButton.Pin_1, DeleteAllImagesButton.Pin_2, R5.Pin_0
  N16: GalleryLeftButton.Pin_1, GalleryLeftButton.Pin_2, R4.Pin_0
  N17: StartMirrorSlideshow.Pin_1, StartMirrorSlideshow.Pin_2, R7.Pin_0
  N18: StartMirrorSlideshow.Pin_3, StartMirrorSlideshow.Pin_4, StartMirrorDefault.Pin_3, StartMirrorDefault.Pin_4, ShutDownMirror.Pin_3, ShutDownMirror.Pin_4
  N19: StartMirrorDefault.Pin_1, StartMirrorDefault.Pin_2, R6.Pin_0
  N20: ShutDownMirror.Pin_1, ShutDownMirror.Pin_2, R8.Pin_0

custom parts:
  HC-SR501 Body Sensor Module: Pyroelectric Infrared PIR Motion Sensor Detector Module
